// Logisim project 10 Bit ALU.circ as structural Verilog: 1 circuit, main circuit main
// 10 Bit ALU
module main (
  input  AInvert,
  input  BInvert,
  input  Cin,
  input  [9:0] INPUT_1,
  input  [9:0] INPUT_2,
  input  [1:0] ALU_Select,
  output Zero,
  output [9:0] Result,
  output Cout
);

  wire main_1_cout, main_2_set;

  _5Bit_LSB_ALU_main main_1 (
    .LESS(main_2_set), .INPUT_1(INPUT_1[4:0]), .INPUT_2(INPUT_2[4:0]), .Result(Result[4:0]),
    .AInvert(AInvert), .BInvert(BInvert), .Cin(Cin), .ALU_Select(ALU_Select), .Cout(main_1_cout));
  _5_Bit_MSB_ALU_main main_2 (
    .INPUT_1(INPUT_1[9:5]), .INPUT_2(INPUT_2[9:5]), .Result(Result[9:5]), .Set(main_2_set),
    .AInvert(AInvert), .BInvert(BInvert), .Cin(main_1_cout), .ALU_Select(ALU_Select), .Cout(Cout));
  nor nor_1 (Zero, Result[0], Result[1], Result[2], Result[3], Result[4], Result[5], Result[6], Result[7], Result[8], Result[9]);
endmodule
