// Logisim project 10 Bit CPU.circ as structural Verilog: 1 circuit, main circuit main
module main (
  input  in_1
);

  wire clock_1_out, main_1_alusrcim, main_1_alusrcj, main_1_alusrcr1, main_1_alusrcr2, main_1_memtoreg,
       main_1_memwrite, main_1_pcsrc, main_1_regdest, main_1_regwrite, main_3_zero, main_4_ainvert,
       main_4_binvert;
  wire [2:0] main_1_aluop, main_4_aluselect, multiplexer_1_out, multiplexer_2_out, multiplexer_3_out;
  wire [9:0] adder_1_out, adder_2_out, bit_extender_1_out, bit_extender_2_out, main_2_ac, main_2_r1_data,
       main_2_r2_data, main_3_result, multiplexer_4_out, multiplexer_5_out, multiplexer_6_out,
       multiplexer_7_out, PC_q, ram_1_data, rom_1_data;

  Clock clock_1 (.out(clock_1_out));
  Register #(.width(10)) PC (.D(multiplexer_6_out), .en(1'b1), .Q(PC_q), .clk(clock_1_out), .clr(in_1));
  Adder #(.width(10)) adder_1 (.a(10'h1), .b(PC_q), .out(adder_1_out));  // open: cin, cout
  ROM #(.addrWidth(10), .dataWidth(10)) rom_1 (.addr(PC_q), .data(rom_1_data), .sel(1'b1));
  // Probe on main_1_regdest
  // Probe on main_1_alusrcr1
  // Probe on main_1_alusrcr2
  Multiplexer #(.width(3), .disabled(0), .enable("false")) multiplexer_1 (
    .in0(rom_1_data[2:0]), .in1(3'b001), .out(multiplexer_1_out), .sel(main_1_alusrcr2));
  Multiplexer #(.width(3), .disabled(0), .enable("false")) multiplexer_2 (
    .in0(3'b001), .in1(rom_1_data[2:0]), .out(multiplexer_2_out), .sel(main_1_regdest));
  assign bit_extender_1_out = {{4{rom_1_data[5]}}, rom_1_data[5:0]};  // Bit_Extender bit_extender_1
  assign bit_extender_2_out = {{7{1'b0}}, rom_1_data[2:0]};  // Bit_Extender bit_extender_2
  Control_main main_1 (
    .OPCODE(rom_1_data[9:6]), .Zero(main_3_zero), .PCSrc(main_1_pcsrc), .ALUSrcR1(main_1_alusrcr1),
    .ALUSrcR2(main_1_alusrcr2), .RegDest(main_1_regdest), .RegWrite(main_1_regwrite),
    .ALUSrcIm(main_1_alusrcim), .ALUSrcJ(main_1_alusrcj), .MemWrite(main_1_memwrite),
    .MemtoReg(main_1_memtoreg), .ALUOp(main_1_aluop));
  Multiplexer #(.width(3), .disabled(0), .enable("false")) multiplexer_3 (
    .in0(rom_1_data[5:3]), .in1(3'b001), .out(multiplexer_3_out), .sel(main_1_alusrcr1));
  // Probe on main_1_regwrite
  RegisterFile_main main_2 (
    .WRITE_DATA(multiplexer_7_out), .R1_ADDRESS(multiplexer_3_out), .R2_ADDRESS(multiplexer_1_out),
    .AC(main_2_ac), .R1_DATA(main_2_r1_data), .R2_DATA(main_2_r2_data), .RegWrite(main_1_regwrite),
    .Write_Register(multiplexer_2_out), .CLK(clock_1_out));
  Adder #(.width(10)) adder_2 (.a(adder_1_out), .b(bit_extender_1_out), .out(adder_2_out), .cin(1'b0));  // open: cout
  // Probe on main_1_alusrcim
  Multiplexer #(.width(10), .disabled(0), .enable("false")) multiplexer_4 (
    .in0(main_2_r2_data), .in1(bit_extender_2_out), .out(multiplexer_4_out), .sel(main_1_alusrcim));
  // Probe on main_1_alusrcj
  Multiplexer #(.width(10), .disabled(0), .enable("false")) multiplexer_5 (
    .in0(multiplexer_4_out), .in1(bit_extender_1_out), .out(multiplexer_5_out), .sel(main_1_alusrcj));
  Multiplexer #(.width(10), .disabled(0), .enable("false")) multiplexer_6 (
    .in0(adder_1_out), .in1(adder_2_out), .out(multiplexer_6_out), .sel(main_1_pcsrc));
  // Probe on main_1_pcsrc
  // Probe on main_4_ainvert
  // Probe on main_4_aluselect
  // Probe on main_1_memtoreg
  Multiplexer #(.width(10), .disabled(0), .enable("false")) multiplexer_7 (
    .in0(main_3_result), .in1(ram_1_data), .out(multiplexer_7_out), .sel(main_1_memtoreg));
  // Probe on main_4_binvert
  ALU_main main_3 (
    .INPUT_1(main_2_r1_data), .INPUT_2(multiplexer_5_out), .Result(main_3_result), .AInvert(main_4_ainvert),
    .BInvert(main_4_binvert), .ALU_Select(main_4_aluselect), .Zero(main_3_zero));
  ALUControl_main main_4 (
    .ALUOp(main_1_aluop), .ALUSelect(main_4_aluselect), .BInvert(main_4_binvert), .AInvert(main_4_ainvert));
  // Probe on main_1_memwrite
  RAM #(.addrWidth(10), .dataWidth(10), .bus("separate")) ram_1 (
    .addr(main_3_result), .din(main_2_ac), .data(ram_1_data), .str(main_1_memwrite), .sel(1'b1),
    .clk(clock_1_out), .ld(1'b1));  // open: clr

  // Notes on the sheet:
  //   contents of rom_1 (hex, n*v repeats v):
  //   100 c5 0 81 101 c6 3ae c2 0 82 c3 2 143
endmodule
