// Logisim project 1Bit ALU.circ as structural Verilog: 1 circuit, main circuit main
// 1 Bit ALU
module main (
  input  AInvert,
  input  INPUT_1,
  input  Cin,
  input  BInvert,
  input  INPUT_2,
  input  [1:0] ALU_Select,
  input  LESS,
  output Cout,
  output Result
);

  wire adder_1_out, and_1_out, multiplexer_1_out, multiplexer_2_out, not_1_out, not_2_out, or_1_out;

  Multiplexer #(.disabled(0), .enable("false")) multiplexer_1 (
    .in0(INPUT_1), .in1(not_1_out), .out(multiplexer_1_out), .sel(AInvert));
  not not_1 (not_1_out, INPUT_1);
  Multiplexer #(.disabled(0), .enable("false")) multiplexer_2 (
    .in0(INPUT_2), .in1(not_2_out), .out(multiplexer_2_out), .sel(BInvert));
  not not_2 (not_2_out, INPUT_2);
  Adder #(.width(1)) adder_1 (.a(multiplexer_1_out), .b(multiplexer_2_out), .out(adder_1_out), .cin(Cin), .cout(Cout));
  and and_1 (and_1_out, multiplexer_1_out, multiplexer_2_out);
  or or_1 (or_1_out, multiplexer_1_out, multiplexer_2_out);
  Multiplexer #(.select(2), .disabled(0), .enable("false")) multiplexer_3 (
    .in0(adder_1_out), .in1(and_1_out), .in2(or_1_out), .in3(LESS), .out(Result), .sel(ALU_Select));
endmodule
