// Logisim project 5 Bit MSB ALU.circ as structural Verilog: 1 circuit, main circuit main
// 5 Bit MSB ALU
module main (
  input  AInvert,
  input  BInvert,
  input  Cin,
  input  [4:0] INPUT_1,
  input  [4:0] INPUT_2,
  input  [1:0] ALU_Select,
  output [4:0] Result,
  output Set,
  output Cout
);

  wire main_1_cout, main_2_cout, main_3_cout, main_4_cout;

  _1Bit_ALU_main main_1 (
    .INPUT_1(INPUT_1[0]), .INPUT_2(INPUT_2[0]), .LESS(1'b0), .AInvert(AInvert), .BInvert(BInvert), .Cin(Cin),
    .Cout(main_1_cout), .ALU_Select(ALU_Select), .Result(Result[0]));
  _1Bit_ALU_main main_2 (
    .INPUT_1(INPUT_1[1]), .INPUT_2(INPUT_2[1]), .LESS(1'b0), .AInvert(AInvert), .BInvert(BInvert),
    .Cin(main_1_cout), .Cout(main_2_cout), .ALU_Select(ALU_Select), .Result(Result[1]));
  _1Bit_ALU_main main_3 (
    .INPUT_1(INPUT_1[2]), .INPUT_2(INPUT_2[2]), .LESS(1'b0), .AInvert(AInvert), .BInvert(BInvert),
    .Cin(main_2_cout), .Cout(main_3_cout), .ALU_Select(ALU_Select), .Result(Result[2]));
  _1Bit_ALU_main main_4 (
    .INPUT_1(INPUT_1[3]), .INPUT_2(INPUT_2[3]), .LESS(1'b0), .AInvert(AInvert), .BInvert(BInvert),
    .Cin(main_3_cout), .Cout(main_4_cout), .ALU_Select(ALU_Select), .Result(Result[3]));
  _1Bit_MSB_ALU_main main_5 (
    .INPUT_1(INPUT_1[4]), .INPUT_2(INPUT_2[4]), .LESS(1'b0), .AInvert(AInvert), .BInvert(BInvert),
    .Cin(main_4_cout), .Cout(Cout), .ALU_Select(ALU_Select), .Set(Set), .Result(Result[4]));
endmodule
