// Logisim project ALU.circ as structural Verilog: 1 circuit, main circuit main
// ALU
module main (
  input  AInvert,
  input  BInvert,
  input  [9:0] INPUT_1,
  input  [9:0] INPUT_2,
  input  [2:0] ALU_Select,
  output Zero,
  output [9:0] Result
);

  wire [9:0] main_1_shift_result, main_2_result;

  Shifter_main main_1 (
    .INPUT_1(INPUT_1), .INPUT_2(INPUT_2), .Shift_Result(main_1_shift_result), .Shift_Select(ALU_Select[1]));
  _10_Bit_ALU_main main_2 (
    .INPUT_1(INPUT_1), .INPUT_2(INPUT_2), .Result(main_2_result), .AInvert(AInvert), .BInvert(BInvert),
    .Cin(BInvert), .ALU_Select(ALU_Select[1:0]), .Zero(Zero));  // open: Cout
  Multiplexer #(.width(10), .disabled(0), .enable("false")) multiplexer_1 (
    .in0(main_2_result), .in1(main_1_shift_result), .out(Result), .sel(ALU_Select[2]));
endmodule
