// Logisim project ALUControl.circ as structural Verilog: 1 circuit, main circuit main
// ALUControl
module main (
  input  [2:0] ALUOp,
  output AInvert,
  output [2:0] ALUSelect,
  output BInvert
);

  wire decoder_1_out1, decoder_1_out2, decoder_1_out3, decoder_1_out5, decoder_1_out6, decoder_1_out7;

  Decoder #(.select(3), .disabled(0), .enable("false")) decoder_1 (
    .out1(decoder_1_out1), .out2(decoder_1_out2), .out3(decoder_1_out3), .out4(AInvert),
    .out5(decoder_1_out5), .out6(decoder_1_out6), .out7(decoder_1_out7), .sel(ALUOp));  // open: out0
  or or_1 (ALUSelect[2], decoder_1_out6, decoder_1_out5);
  or or_2 (ALUSelect[0], decoder_1_out7, AInvert, decoder_1_out2);
  or or_3 (ALUSelect[1], decoder_1_out7, decoder_1_out6, decoder_1_out3);
  or or_4 (BInvert, decoder_1_out1, decoder_1_out7, AInvert);
endmodule
