// Logisim project Control.circ as structural Verilog: 1 circuit, main circuit main
// Control
module main (
  input  [3:0] OPCODE,
  input  Zero,
  output [2:0] ALUOp,
  output MemtoReg,
  output MemWrite,
  output ALUSrcJ,
  output ALUSrcIm,
  output RegWrite,
  output RegDest,
  output ALUSrcR2,
  output PCSrc,
  output ALUSrcR1
);

  wire decoder_1_out0, decoder_1_out1, decoder_1_out2, decoder_1_out6, decoder_1_out7, decoder_1_out8,
       decoder_1_out9, decoder_1_out10, decoder_1_out11, decoder_1_out12, decoder_1_out13, decoder_1_out14,
       decoder_1_out15, multiplexer_1_out;

  Decoder #(.select(4), .disabled(0), .enable("false")) decoder_1 (
    .out0(decoder_1_out0), .out1(decoder_1_out1), .out2(decoder_1_out2), .out3(RegDest), .out4(MemtoReg),
    .out5(MemWrite), .out6(decoder_1_out6), .out7(decoder_1_out7), .out8(decoder_1_out8),
    .out9(decoder_1_out9), .out10(decoder_1_out10), .out11(decoder_1_out11), .out12(decoder_1_out12),
    .out13(decoder_1_out13), .out14(decoder_1_out14), .out15(decoder_1_out15), .sel(OPCODE));
  Multiplexer #(.disabled(0), .enable("false")) multiplexer_1 (
    .in0(decoder_1_out12), .in1(decoder_1_out11), .out(multiplexer_1_out), .sel(Zero));
  or or_1 (PCSrc, decoder_1_out13, multiplexer_1_out);
  or or_2 (ALUSrcR1, decoder_1_out2, decoder_1_out11, decoder_1_out12, decoder_1_out15);
  or or_3 (ALUSrcR2, RegDest, decoder_1_out11, decoder_1_out12);
  or or_4 (RegWrite, decoder_1_out0, decoder_1_out1, decoder_1_out2, RegDest, MemtoReg, decoder_1_out15, decoder_1_out6, decoder_1_out7, decoder_1_out8, decoder_1_out9, decoder_1_out10, decoder_1_out14);
  or or_5 (ALUSrcIm, decoder_1_out8, decoder_1_out9);
  or or_6 (ALUSrcJ, decoder_1_out2, decoder_1_out15);
  or or_7 (ALUOp[2], decoder_1_out8, decoder_1_out9, decoder_1_out14, decoder_1_out15);
  or or_8 (ALUOp[1], decoder_1_out6, decoder_1_out7, decoder_1_out9, decoder_1_out10, decoder_1_out11, decoder_1_out12, decoder_1_out14, decoder_1_out15);
  or or_9 (ALUOp[0], decoder_1_out1, decoder_1_out7, decoder_1_out8, decoder_1_out14, decoder_1_out15);
endmodule
