// Logisim project RegisterFile.circ as structural Verilog: 1 circuit, main circuit main
// Register File
module main (
  input  [9:0] WRITE_DATA,
  input  [2:0] Write_Register,
  input  RegWrite,
  input  [2:0] R1_ADDRESS,
  input  [2:0] R2_ADDRESS,
  input  CLK,
  output [9:0] AC,
  output [9:0] R1_DATA,
  output [9:0] R2_DATA
);

  wire decoder_1_out1, decoder_1_out2, decoder_1_out3, decoder_1_out4, decoder_1_out5, decoder_1_out6,
       decoder_1_out7;
  wire [9:0] S0_q, S1_q, S2_q, T0_q, T1_q, T2_q;

  Decoder #(.select(3), .disabled(0)) decoder_1 (
    .out1(decoder_1_out1), .out2(decoder_1_out2), .out3(decoder_1_out3), .out4(decoder_1_out4),
    .out5(decoder_1_out5), .out6(decoder_1_out6), .out7(decoder_1_out7), .sel(Write_Register), .en(RegWrite));  // open: out0
  Register #(.width(10)) u_AC (.D(WRITE_DATA), .en(decoder_1_out1), .Q(AC), .clk(CLK));  // open: clr
  Register #(.width(10)) T0 (.D(WRITE_DATA), .en(decoder_1_out2), .Q(T0_q), .clk(CLK));  // open: clr
  Register #(.width(10)) T1 (.D(WRITE_DATA), .en(decoder_1_out3), .Q(T1_q), .clk(CLK));  // open: clr
  Register #(.width(10)) T2 (.D(WRITE_DATA), .en(decoder_1_out4), .Q(T2_q), .clk(CLK));  // open: clr
  Register #(.width(10)) S0 (.D(WRITE_DATA), .en(decoder_1_out5), .Q(S0_q), .clk(CLK));  // open: clr
  Register #(.width(10)) S1 (.D(WRITE_DATA), .en(decoder_1_out6), .Q(S1_q), .clk(CLK));  // open: clr
  Register #(.width(10)) S2 (.D(WRITE_DATA), .en(decoder_1_out7), .Q(S2_q), .clk(CLK));  // open: clr
  Multiplexer #(.select(3), .width(10), .disabled(0), .enable("false")) multiplexer_1 (
    .in0({10{1'b0}}), .in1(AC), .in2(T0_q), .in3(T1_q), .in4(T2_q), .in5(S0_q), .in6(S1_q), .in7(S2_q),
    .out(R1_DATA), .sel(R1_ADDRESS));
  Multiplexer #(.select(3), .width(10), .disabled(0), .enable("false")) multiplexer_2 (
    .in0({10{1'b0}}), .in1(AC), .in2(T0_q), .in3(T1_q), .in4(T2_q), .in5(S0_q), .in6(S1_q), .in7(S2_q),
    .out(R2_DATA), .sel(R2_ADDRESS));
endmodule
