// Logisim project Shifter.circ as structural Verilog: 1 circuit, main circuit main
// Shifter
module main (
  input  [9:0] INPUT_1,
  input  [9:0] INPUT_2,
  input  Shift_Select,
  output [9:0] Shift_Result
);

  wire [9:0] shifter_1_out, shifter_2_out;

  Shifter #(.width(10)) shifter_1 (.in(INPUT_1), .\dist (INPUT_2[3:0]), .out(shifter_1_out));
  Shifter #(.width(10), .shift("lr")) shifter_2 (.in(INPUT_1), .\dist (INPUT_2[3:0]), .out(shifter_2_out));
  Multiplexer #(.width(10), .disabled(0), .enable("false")) multiplexer_1 (
    .in0(shifter_1_out), .in1(shifter_2_out), .out(Shift_Result), .sel(Shift_Select));
endmodule
